# Fritzing sketch Power_1 (saved by Fritzing 0.9.3b)

parts:
  Componente2 = TP4056 Charger
  U1 = Mystery Part - 2 pins [chip_label=? package=THT]
  BAT1 = 18650 battery holder [package=battery-18650-kit]
  S1 = Toggle Switch [package=THT]
  J1 = Power Plug

nets:
  N1: Componente2.BAT+, U1.VIN+, S1.COM
  N2: Componente2.BAT-, U1.VIN-, BAT1.-
  N3: U1.VOUT+, J1.PWR
  N4: U1.VOUT-, J1.GND
  N5: BAT1.+, S1.L2

custom parts:
  Mystery Part - 2 pins: A dummy, proxy, ersatz, stand-in part for whatever you want. With 2 pins on a 100 mil inline pin header footprint.
  18650 battery holder: 18650 Battery Holder
  Power Plug: Power Jack This is the standard 5.5mm barrel plug for power. This part has bendable leads (i.e. wires in the real world) to connect to wall warts or the breadboard in the standard wire end, and hidden connectors on the tip end that will connect when "plugged in" (overlapped with the jack so it appears "plugged in" in breadboard) to the modified coax jack part. Internal busses connect the two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
